// Logisim project scheme.circ as structural Verilog: 1 circuit, main circuit main
module main (
);

  wire and_1_out, and_2_out, and_3_out, and_4_out, and_5_out, and_6_out, and_7_out, and_8_out, and_9_out,
       and_10_out, and_11_out, and_12_out, and_13_out, in_s0_prime_out, in_s1_prime_out, in_s2_prime_out,
       in_s3_prime_out, out_s1_out, out_s2_out, out_s3_out, out_s4_out, out_s5_out, out_s6_out, out_s7_out;

  not in_s3_prime (in_s3_prime_out, 1'b1);
  not in_s2_prime (in_s2_prime_out, 1'b0);
  not in_s1_prime (in_s1_prime_out, 1'b0);
  not in_s0_prime (in_s0_prime_out, 1'b1);
  and and_1 (and_1_out, 1'b0, in_s1_prime_out, in_s0_prime_out);
  and and_2 (and_2_out, in_s3_prime_out, in_s2_prime_out, in_s1_prime_out, 1'b1);
  and and_3 (and_3_out, 1'b0, in_s1_prime_out, 1'b1);
  and and_4 (and_4_out, 1'b0, 1'b0, in_s0_prime_out);
  and and_5 (and_5_out, in_s3_prime_out, in_s2_prime_out, in_s1_prime_out, 1'b1);
  and and_6 (and_6_out, 1'b0, in_s1_prime_out, in_s0_prime_out);
  and and_7 (and_7_out, 1'b0, 1'b0, 1'b1);
  and and_8 (and_8_out, 1'b0, in_s1_prime_out);
  and and_9 (and_9_out, in_s3_prime_out, in_s2_prime_out, 1'b1);
  and and_10 (and_10_out, in_s3_prime_out, in_s2_prime_out, 1'b0);
  and and_11 (and_11_out, 1'b0, 1'b1);
  and and_12 (and_12_out, in_s3_prime_out, in_s2_prime_out, in_s1_prime_out);
  and and_13 (and_13_out, 1'b0, 1'b0, 1'b1);
  or out_s7 (out_s7_out, and_1_out, and_2_out);
  or out_s6 (out_s6_out, and_3_out, and_4_out);
  and out_s5 (out_s5_out, in_s2_prime_out, 1'b0, in_s0_prime_out);
  or out_s4 (out_s4_out, and_5_out, and_6_out, and_7_out);
  or out_s3 (out_s3_out, 1'b1, and_8_out);
  or out_s2 (out_s2_out, and_9_out, and_10_out, and_11_out);
  or out_s1 (out_s1_out, and_12_out, and_13_out);
  _7_Segment_Display #(.active("false")) u_7_segment_display_1 (
    .g(out_s1_out), .f(out_s2_out), .a(out_s7_out), .b(out_s6_out), .e(out_s3_out), .d(out_s4_out),
    .c(out_s5_out), .dp(1'b1));
endmodule
